// Logisim project Basic_Comp_2018_26515.circ as structural Verilog: 4 circuits, main circuit main
module main (
  input  in_1,
  input  in_2,
  input  in_3,
  input  in_4,
  input  in_5,
  input  in_6,
  input  Start,
  input  Restart,
  input  in_9,
  input  in_10,
  input  in_11
);

  wire ADO, ALU_eout, AND, CLK, clock_1_out, clrs, controlled_buffer_1_out, d_ff_1_q, d_ff_2_q, FGI, FGO,
       IAC, IEN, IPC, LAC, LAR, LDR, LIR, not_1_out, READMEM, SCL, SCR, T0, T1, T2, TO, WM;
  wire [2:0] lcu_1_busscon;
  wire [7:0] bit_extender_1_out, INPR_q;
  wire [11:0] AR12, AR_q, bit_extender_2_out, bit_extender_3_out, PC_q;
  wire [15:0] AC_q, ALU_ac_2, bit_extender_4_out, bit_extender_5_out, DR_q, IR, multiplexer_1_out, ram_1_data;

  Clock clock_1 (.out(clock_1_out));
  D_Flip_Flop d_ff_1 (.Q(d_ff_1_q), .preset(controlled_buffer_1_out), .reset(clrs));  // open: clk, D, Qn, en
  assign controlled_buffer_1_out = not_1_out ? Start : 1'bz;  // Controlled_Buffer controlled_buffer_1
  not not_1 (not_1_out, clrs);
  and and_1 (CLK, clock_1_out, d_ff_1_q);
  Bit_Extender #(.in_width(16), .out_width(8)) bit_extender_1 (.in(multiplexer_1_out), .out(bit_extender_1_out));
  ALU ALU (
    .AC(AC_q), .DR(DR_q), .INPR(INPR_q), .Ein(d_ff_2_q), .in_1(in_4), .in_2(SCL), .in_3(SCR), .in_4(in_3),
    .in_5(TO), .in_6(ADO), .in_7(AND), .Eout(ALU_eout), .AC_2(ALU_ac_2));
  Bit_Extender #(.in_width(16), .out_width(12)) bit_extender_2 (.in(multiplexer_1_out), .out(bit_extender_2_out));
  Bit_Extender #(.in_width(16), .out_width(12)) bit_extender_3 (.in(multiplexer_1_out), .out(bit_extender_3_out));
  D_Flip_Flop d_ff_2 (.clk(CLK), .D(ALU_eout), .Q(d_ff_2_q));  // open: Qn, preset, en, reset
  Counter #(.width(12), .max('hfff)) AR (
    .load(LAR), .D(bit_extender_2_out), .count(in_5), .Q(AR_q), .clk(CLK), .clr(clrs));  // open: carry
  Counter #(.width(12), .max('hfff)) PC (
    .load(in_2), .D(bit_extender_3_out), .count(IPC), .Q(PC_q), .clk(CLK), .clr(clrs));  // open: carry
  Counter #(.width(16), .max('hffff)) DR (
    .load(LDR), .D(multiplexer_1_out), .count(in_6), .Q(DR_q), .clk(CLK), .clr(clrs));  // open: carry
  Counter #(.width(16), .max('hffff)) AC (
    .load(LAC), .D(ALU_ac_2), .count(IAC), .Q(AC_q), .clk(CLK), .clr(clrs));  // open: carry
  Register INPR (.en(in_9), .Q(INPR_q), .clk(CLK), .clr(clrs));  // open: D
  Counter #(.width(16), .max('hffff)) u_IR (
    .load(LIR), .D(multiplexer_1_out), .count(in_10), .Q(IR), .clk(CLK), .clr(Restart));  // open: carry
  Counter OUTR (.load(in_1), .D(bit_extender_1_out), .count(in_11), .clk(CLK), .clr(clrs));  // open: Q, carry
  RAM #(.addrWidth(12), .dataWidth(16), .bus("separate")) ram_1 (
    .addr(AR_q), .din(multiplexer_1_out), .data(ram_1_data), .str(WM), .clk(CLK), .ld(READMEM));  // open: sel, clr
  assign bit_extender_4_out = {{4{1'b0}}, AR_q};  // Bit_Extender bit_extender_4
  assign bit_extender_5_out = {{4{1'b0}}, PC_q};  // Bit_Extender bit_extender_5
  Multiplexer #(.select(3), .width(16), .enable("false")) multiplexer_1 (
    .in1(bit_extender_4_out), .in2(bit_extender_5_out), .in3(DR_q), .in4(AC_q), .in5(IR), .in7(ram_1_data),
    .out(multiplexer_1_out), .sel(lcu_1_busscon));  // open: in0, in6
  LCU lcu_1 (
    .CLK(CLK), .IR(IR), .READMEM(READMEM), .CLRS(clrs), .start(Start), .ANDOP(AND), .ADDOPCARYINE(ADO),
    .SCR(SCR), .SCL(SCL), .LDIR(LIR), .LDAC(LAC), .LDAR(LAR), .AR12(AR12), .INCPC(IPC), .TRANSOP(TO),
    .WRITEMEM(WM), .LDDR(LDR), .INCAC(IAC), .BUSSCON(lcu_1_busscon));
  I_O i_o_1 (
    .IEN(IEN), .CLK(CLK), .FGI(FGI), .T0(T0), .FGO(FGO), .T1(T1), .T2(T2));  // open: R, PCBUSS, TRBUSS, CLRCS, LDTR, MEMWR, CLRAR, INCPC, CLRPC
endmodule

module ALU (
  input  in_1,
  input  in_2,
  input  in_3,
  input  in_4,
  input  in_5,
  input  in_6,
  input  in_7,
  input  [15:0] AC,
  input  [15:0] DR,
  input  [7:0] INPR,
  input  Ein,
  output [15:0] AC_2,
  output Eout
);

  wire adder_1_cout, not_2_out;
  wire [1:0] bit_extender_1_out, or_1_out;
  wire [2:0] priority_encoder_1_out;
  wire [15:0] adder_1_out, and_1_out, bit_extender_2_out, not_1_out;

  Priority_Encoder priority_encoder_1 (
    .in0(in_7), .in1(in_6), .in2(in_5), .in3(in_4), .in4(in_3), .in5(in_2), .in6(in_1),
    .out(priority_encoder_1_out));  // open: in7, en_in, gs, en_out
  assign and_1_out = AC & DR;  // AND_Gate and_1, 16 bits wide
  assign bit_extender_1_out = {{1{in_6}}, in_6};  // Bit_Extender bit_extender_1
  Adder #(.width(16)) adder_1 (.a(AC), .b(DR), .out(adder_1_out), .cout(adder_1_cout));  // open: cin
  assign bit_extender_2_out = {{8{1'b0}}, INPR};  // Bit_Extender bit_extender_2
  Multiplexer #(.select(3), .width(16), .enable("false")) multiplexer_1 (
    .in0(and_1_out), .in1(adder_1_out), .in2(DR), .in3(bit_extender_2_out), .in4(not_1_out),
    .in5({Ein, AC[15:1]}), .in6({AC[14:0], Ein}), .out(AC_2), .sel(priority_encoder_1_out));  // open: in7
  assign not_1_out = ~AC;  // NOT_Gate not_1, 16 bits wide
  assign or_1_out = bit_extender_1_out | {in_1, in_2};  // OR_Gate or_1, 2 bits wide
  Multiplexer #(.select(2), .disabled(0), .enable("false")) multiplexer_2 (
    .in0(not_2_out), .in1(AC[0]), .in2(AC[15]), .in3(adder_1_cout), .out(Eout), .sel(or_1_out));
  not not_2 (not_2_out, 1'b1);
endmodule

module LCU (
  input  CLK,
  input  [15:0] IR,
  input  start,
  output ANDOP,
  output ADDOPCARYINE,
  output SCR,
  output SCL,
  output LDIR,
  output LDAC,
  output LDAR,
  output [11:0] AR12,
  output INCPC,
  output TRANSOP,
  output WRITEMEM,
  output LDDR,
  output INCAC,
  output READMEM,
  output CLRS,
  output [2:0] BUSSCON
);

  wire ACINBUSS, and_2_out, and_6_out, and_7_out, and_8_out, and_9_out, and_10_out, and_11_out, and_12_out,
       and_13_out, and_14_out, and_16_out, and_18_out, and_19_out, and_21_out, and_22_out, CAR, CLRSC, CPC,
       CSC, D0, D1, D2, D3, D4, D5, D6, D7, d_ff_1_q, d_ff_2_q, FGI, FGO, I, IEN, INCSC, IPC, LTR, MW,
       not_1_out, not_2_out, not_3_out, not_4_out, not_5_out, not_6_out, or_1_out, or_2_out, or_3_out,
       or_8_out, or_9_out, or_10_out, PCBUSS, R, T0, T0aT1c, T2, T3, T4, T5, T6, T7, T8, T9, T10, T11, T12,
       T13, T14, T15, TRB;
  wire [2:0] controlled_buffer_2_out;
  wire [3:0] counter_1_q;

  not not_1 (not_1_out, CLRSC);
  D_Flip_Flop d_ff_1 (.clk(CLK), .D(1'b1), .Q(d_ff_1_q), .reset(CLRS));  // open: Qn, preset, en
  and and_1 (INCSC, not_1_out, CLK);
  Counter #(.width(4), .max('hf)) counter_1 (
    .count(and_2_out), .Q(counter_1_q), .clk(CLK), .clr(d_ff_2_q));  // open: load, D, carry
  and and_2 (and_2_out, d_ff_1_q, 1'b1);
  D_Flip_Flop d_ff_2 (.clk(CLK), .D(CLRSC), .Q(d_ff_2_q));  // open: Qn, preset, en, reset
  not not_2 (not_2_out, T0);
  not not_3 (not_3_out, LDIR);
  Decoder #(.select(4)) decoder_1 (
    .out0(T0), .out1(LDIR), .out2(T2), .out3(T3), .out4(T4), .out5(T5), .out6(T6), .out7(T7), .out8(T8),
    .out9(T9), .out10(T10), .out11(T11), .out12(T12), .out13(T13), .out14(T14), .out15(T15), .sel(counter_1_q));  // open: en
  assign AR12 = T0aT1c ? IR[11:0] : 12'bz;  // Controlled_Buffer controlled_buffer_1
  assign controlled_buffer_2_out = T0aT1c ? IR[14:12] : 3'bz;  // Controlled_Buffer controlled_buffer_2
  D_Flip_Flop d_ff_3 (.clk(CLK), .D(IR[15]), .Q(I));  // open: Qn, preset, en, reset
  and and_3 (T0aT1c, not_2_out, not_3_out);
  Decoder #(.select(3)) decoder_2 (
    .out0(D0), .out1(D1), .out2(D2), .out3(D3), .out4(D4), .out5(D5), .out6(D6), .out7(D7),
    .sel(controlled_buffer_2_out));  // open: en
  not not_4 (not_4_out, I);
  and and_4 (R, not_4_out, D7, T3);
  and and_5 (ANDOP, D0, T5);
  or or_1 (or_1_out, D0, D1, D5, D2);
  or or_2 (or_2_out, D3, D4);
  not not_5 (not_5_out, D7);
  and and_6 (and_6_out, D6, T6);
  and and_7 (and_7_out, R, AR12[4]);
  and and_8 (and_8_out, R, AR12[3]);
  and and_9 (and_9_out, R, AR12[2]);
  and and_10 (and_10_out, R, AR12[1]);
  or or_3 (or_3_out, D0, D1, D2, D6);
  not not_6 (not_6_out, D7);
  and and_11 (and_11_out, or_1_out, T5);
  and and_12 (and_12_out, or_2_out, T4);
  and and_13 (and_13_out, D6, T6);
  and and_14 (and_14_out, not_5_out, I, T3);
  and and_15 (LDDR, or_3_out, T4);
  and and_16 (and_16_out, not_6_out, I, T3);
  and and_17 (ADDOPCARYINE, D1, T5);
  or or_4 (LDAR, and_14_out, T0, T2, D5, T4);
  or or_5 (INCPC, and_6_out, and_7_out, and_8_out, and_9_out, and_10_out, LDIR);
  or or_6 (CLRSC, and_11_out, and_12_out, start, and_13_out, R);
  or or_7 (READMEM, LDDR, LDIR, and_16_out);
  or or_8 (or_8_out, D3, D5);
  and and_18 (and_18_out, or_8_out, T4);
  and and_19 (and_19_out, D6, T6);
  and and_20 (SCR, R, AR12[7]);
  or or_9 (or_9_out, D0, D1, D2);
  or or_10 (or_10_out, AR12[7], AR12[6]);
  or or_11 (WRITEMEM, and_18_out, and_19_out);
  and and_21 (and_21_out, or_9_out, T5);
  and and_22 (and_22_out, R, or_10_out);
  and and_23 (ACINBUSS, T4, D3);
  and and_24 (INCAC, R, AR12[5]);
  and and_25 (CLRS, R, AR12[0]);
  Priority_Encoder priority_encoder_1 (
    .in0(1'b0), .in1(1'b0), .in2(T0), .in3(1'b0), .in4(ACINBUSS), .in5(T2), .in6(1'b0), .in7(READMEM),
    .out(BUSSCON));  // open: en_in, gs, en_out
  and and_26 (SCL, R, AR12[6]);
  or or_12 (LDAC, and_21_out, and_22_out);
  and and_27 (TRANSOP, T5, D2);
  I_O i_o_1 (
    .IEN(IEN), .CLK(CLK), .FGI(FGI), .T0(T0), .FGO(FGO), .T1(LDIR), .T2(T2), .R(R), .PCBUSS(PCBUSS),
    .TRBUSS(TRB), .CLRCS(CSC), .LDTR(LTR), .MEMWR(MW), .CLRAR(CAR), .INCPC(IPC), .CLRPC(CPC));

  // Other names for the same wires on the sheet: B0 = AR12[0]; B1 = AR12[1]; B2 = AR12[2]; B3 = AR12[3]; B4 = AR12[4];
  //   B5 = AR12[5]; B6 = AR12[6]; B7 = AR12[7]; B8 = AR12[8]; B9 = AR12[9]; B10 = AR12[10]; B11 = AR12[11]; T1 = LDIR
endmodule

module I_O (
  input  IEN,
  input  CLK,
  input  FGI,
  input  T0,
  input  FGO,
  input  T1,
  input  T2,
  output PCBUSS,
  output LDTR,
  output CLRAR,
  output TRBUSS,
  output MEMWR,
  output CLRPC,
  output CLRCS,
  output INCPC,
  output R
);

  wire and_1_out, FGI_t, FGO_t, IEN_t, not_1_out, not_2_out, not_3_out, or_1_out;

  or or_1 (or_1_out, FGI_t, FGO_t);
  not not_1 (not_1_out, T0);
  not not_2 (not_2_out, T1);
  not not_3 (not_3_out, T2);
  and and_1 (and_1_out, or_1_out, IEN_t, not_1_out, not_2_out, not_3_out);
  D_Flip_Flop u_IEN (.clk(CLK), .D(IEN), .Q(IEN_t), .reset(CLRCS));  // open: Qn, preset, en
  D_Flip_Flop u_R (.clk(CLK), .D(and_1_out), .Q(R), .reset(CLRCS));  // open: Qn, preset, en
  D_Flip_Flop u_FGI (.clk(CLK), .D(FGI), .Q(FGI_t));  // open: Qn, preset, en, reset
  D_Flip_Flop u_FGO (.clk(CLK), .D(FGO), .Q(FGO_t));  // open: Qn, preset, en, reset
  and and_2 (CLRAR, T0, R);
  and and_3 (CLRPC, T1, R);
  and and_4 (CLRCS, T2, R);

  assign INCPC = CLRCS;
  assign LDTR = CLRAR;
  assign MEMWR = CLRPC;
  assign PCBUSS = CLRAR;
  assign TRBUSS = CLRPC;

  // Other names for the same wires on the sheet: CLRIEN = CLRCS; CLRR = CLRCS
endmodule
