// Logisim project bus system (2).circ as structural Verilog: 2 circuits, main circuit main
module main (
);

  wire clock_1_out;
  wire [2:0] undriven;
  wire [7:0] _1, _6;
  wire [11:0] _4, _5;
  wire [11:8] _2;
  wire [15:0] AC_q, DR_q, IR_q, ram_1_data;
  wire [15:12] _7, _8, _9;

  Counter INPR (.Q(_6), .clk(clock_1_out));  // open: load, D, count, carry, clr
  Clock clock_1 (.out(clock_1_out));
  Counter OUTR (.D(_1), .clk(clock_1_out));  // open: load, count, Q, carry, clr
  Counter #(.width(16), .max('hffff)) AC (.Q(AC_q), .clk(clock_1_out));  // open: load, D, count, carry, clr
  Counter #(.width(12), .max('hfff)) AR (.D({_2, _1}), .Q(_4), .clk(clock_1_out));  // open: load, count, carry, clr
  Counter #(.width(16), .max('hffff)) IR (
    .D({_7, _2, _1}), .Q(IR_q), .clk(clock_1_out));  // open: load, count, carry, clr
  Counter #(.width(16), .max('hffff)) DR (
    .D({_7, _2, _1}), .Q(DR_q), .clk(clock_1_out));  // open: load, count, carry, clr
  Counter #(.width(12), .max('hfff)) PC (.D({_2, _1}), .Q(_5), .clk(clock_1_out));  // open: load, count, carry, clr
  Multiplexer #(.select(3), .width(16), .enable("false")) multiplexer_1 (
    .in1({_8, _4}), .in2({_9, _5}), .in3(DR_q), .in4(AC_q), .in5(IR_q), .in7(ram_1_data), .out({_7, _2, _1}),
    .sel(undriven));  // open: in0, in6
  RAM #(.addrWidth(12), .dataWidth(16), .bus("separate")) ram_1 (
    .addr(_4), .data(ram_1_data), .clk(clock_1_out));  // open: din, str, sel, ld, clr

  // Other names for the same wires on the sheet: _2[7:0] = _1; _3[11:0] = {_2, _1}; _7[11:0] = {_2, _1};
  //   _8[11:0] = _4; _9[11:0] = _5
endmodule

module ALU (
  input  [15:0] AC,
  input  [7:0] INP,
  input  [15:0] DR,
  input  in_4,
  input  in_5,
  input  in_6,
  output [15:0] out_7,
  output out_8
);

  wire [15:0] adder_1_out, and_1_out, not_1_out;
  wire [15:8] _2;

  assign and_1_out = AC & DR;  // AND_Gate and_1, 16 bits wide
  Adder #(.width(16)) adder_1 (.a(AC), .b(DR), .out(adder_1_out), .cout(out_8));  // open: cin
  assign not_1_out = ~AC;  // NOT_Gate not_1, 16 bits wide
  Multiplexer #(.select(3), .width(16)) multiplexer_1 (
    .in1(and_1_out), .in2(adder_1_out), .in3(DR), .in4({_2, INP}), .in5(not_1_out), .out(out_7),
    .sel({in_6, in_5, in_4}), .en(1'b1));  // open: in0, in6, in7

  // Other names for the same wires on the sheet: _1[7:0] = INP; _2[7:0] = INP
endmodule
