// Logisim project bus system (4).circ as structural Verilog: 2 circuits, main circuit main
module main (
  input  LDOUTR,
  input  S2R,
  input  S1R,
  input  S0R,
  input  LDIR,
  input  LDAC,
  input  INCAC,
  input  XLRAC,
  input  LDDR,
  input  INCDR,
  input  CLRDR,
  input  LDOC,
  input  INCPC,
  input  CLRPC,
  input  LDAR,
  input  INCAR,
  input  CLRAR,
  input  S0O,
  input  S1O,
  input  S2O,
  input  WRITE,
  input  READ
);

  wire alu_1_off, clock_1_out, d_ff_1_q;
  wire [7:0] _1, _6;
  wire [11:0] _4, _5;
  wire [11:8] _2;
  wire [15:0] _10, _11, _12, IR_q, ram_1_data;
  wire [15:12] _7, _8, _9;

  Counter INPR (.count(1'b0), .Q(_6), .clk(clock_1_out));  // open: load, D, carry, clr
  Clock clock_1 (.out(clock_1_out));
  Counter OUTR (.load(LDOUTR), .D(_1), .count(1'b0), .clk(clock_1_out));  // open: Q, carry, clr
  Counter #(.width(16), .max('hffff)) AC (
    .load(LDAC), .D(_12), .count(INCAC), .Q(_10), .clk(clock_1_out), .clr(XLRAC));  // open: carry
  Counter #(.width(12), .max('hfff)) AR (
    .load(LDAR), .D({_2, _1}), .count(INCAR), .Q(_4), .clk(clock_1_out), .clr(CLRAR));  // open: carry
  Counter #(.width(16), .max('hffff)) IR (
    .load(LDIR), .D({_7, _2, _1}), .count(1'b0), .Q(IR_q), .clk(clock_1_out));  // open: carry, clr
  Counter #(.width(16), .max('hffff)) DR (
    .load(LDDR), .D({_7, _2, _1}), .count(INCDR), .Q(_11), .clk(clock_1_out), .clr(CLRDR));  // open: carry
  Counter #(.width(12), .max('hfff)) PC (
    .load(LDOC), .D({_2, _1}), .count(INCPC), .Q(_5), .clk(clock_1_out), .clr(CLRPC));  // open: carry
  RAM #(.addrWidth(12), .dataWidth(16), .bus("separate")) ram_1 (
    .addr(_4), .din({_7, _2, _1}), .data(ram_1_data), .str(WRITE), .clk(clock_1_out), .ld(READ));  // open: sel, clr
  Multiplexer #(.select(3), .width(16), .enable("false")) multiplexer_1 (
    .in1({_8, _4}), .in2({_9, _5}), .in3(_11), .in4(_10), .in5(IR_q), .in7(ram_1_data), .out({_7, _2, _1}),
    .sel({S2R, S1R, S0R}));  // open: in0, in6
  ALU alu_1 (.AC(_10), .INP(_6), .DR(_11), .IFF(d_ff_1_q), .OUT(_12), .S0(S0O), .S1(S1O), .S2(S2O), .OFF(alu_1_off));
  D_Flip_Flop d_ff_1 (.clk(clock_1_out), .D(alu_1_off), .Q(d_ff_1_q));  // open: Qn, preset, en, reset

  // Other names for the same wires on the sheet: _2[7:0] = _1; _3[11:0] = {_2, _1}; _7[11:0] = {_2, _1};
  //   _8[11:0] = _4; _9[11:0] = _5
endmodule

module ALU (
  input  [15:0] AC,
  input  [7:0] INP,
  input  [15:0] DR,
  input  S0,
  input  S1,
  input  S2,
  input  IFF,
  output [15:0] OUT,
  output OFF
);

  wire adder_1_cout, xnor_1_out;
  wire [1:0] o1;
  wire [15:0] adder_1_out, and_1_out, not_1_out;
  wire [16:0] _5, _8;

  assign and_1_out = AC & DR;  // AND_Gate and_1, 16 bits wide
  Adder #(.width(16)) adder_1 (.a(AC), .b(DR), .out(adder_1_out), .cin(1'b0), .cout(adder_1_cout));
  Shifter #(.width(17), .shift("rr")) shifter_1 (.in({IFF, AC}), .\dist (5'b00001), .out(_5));
  Shifter #(.width(17), .shift("rl")) shifter_2 (.in({IFF, AC}), .\dist (5'b00001), .out(_8));
  assign not_1_out = ~AC;  // NOT_Gate not_1, 16 bits wide
  Multiplexer #(.select(3), .width(16)) multiplexer_1 (
    .in1(and_1_out), .in2(adder_1_out), .in3(DR), .in4({{8{1'b0}}, INP}), .in5(not_1_out), .in6(_5[15:0]),
    .in7(_8[15:0]), .out(OUT), .sel({S2, S1, S0}), .en(1'b1));  // open: in0
  Multiplexer #(.select(2)) multiplexer_2 (
    .in1(adder_1_cout), .in2(_5[16]), .in3(_8[16]), .out(OFF), .sel(o1));  // open: in0, en
  and and_2 (o1[1], S2, S1);
  xnor xnor_1 (xnor_1_out, S2, S0);
  and and_3 (o1[0], xnor_1_out, S1);

  // Other names for the same wires on the sheet: _1[7:0] = INP; _2[7:0] = INP; _6[15:0] = _5[15:0]; _3[15:0] = AC;
  //   _4[16:0] = {IFF, AC}; _7[16:0] = {IFF, AC}; _9[15:0] = _8[15:0]
endmodule
