// Logisim project bus system.circ as structural Verilog: 1 circuit, main circuit main
module main (
);

  wire clock_1_out;
  wire [2:0] undriven;
  wire [7:0] _1, _6;
  wire [11:0] _4, _5;
  wire [11:8] _2;
  wire [15:0] AC_q, DR_q, IR_q, ram_1_data;
  wire [15:12] _7, _8, _9;

  Counter INPR (.Q(_6), .clk(clock_1_out));  // open: load, D, count, carry, clr
  Clock clock_1 (.out(clock_1_out));
  Counter OUTR (.D(_1), .clk(clock_1_out));  // open: load, count, Q, carry, clr
  Counter #(.width(16), .max('hffff)) AC (.Q(AC_q), .clk(clock_1_out));  // open: load, D, count, carry, clr
  Counter #(.width(12), .max('hfff)) AR (.D({_2, _1}), .Q(_4), .clk(clock_1_out));  // open: load, count, carry, clr
  Counter #(.width(16), .max('hffff)) IR (
    .D({_7, _2, _1}), .Q(IR_q), .clk(clock_1_out));  // open: load, count, carry, clr
  Counter #(.width(16), .max('hffff)) DR (
    .D({_7, _2, _1}), .Q(DR_q), .clk(clock_1_out));  // open: load, count, carry, clr
  Counter #(.width(12), .max('hfff)) PC (.D({_2, _1}), .Q(_5), .clk(clock_1_out));  // open: load, count, carry, clr
  Multiplexer #(.select(3), .width(16), .enable("false")) multiplexer_1 (
    .in1({_8, _4}), .in2({_9, _5}), .in3(DR_q), .in4(AC_q), .in5(IR_q), .in7(ram_1_data), .out({_7, _2, _1}),
    .sel(undriven));  // open: in0, in6
  RAM #(.addrWidth(12), .dataWidth(16), .bus("separate")) ram_1 (
    .addr(_4), .data(ram_1_data), .clk(clock_1_out));  // open: din, str, sel, ld, clr

  // Other names for the same wires on the sheet: _2[7:0] = _1; _3[11:0] = {_2, _1}; _7[11:0] = {_2, _1};
  //   _8[11:0] = _4; _9[11:0] = _5
endmodule
